# Fritzing sketch lights (saved by Fritzing 0.9.3b)
breadboards: 1

parts:
  LED1 = LED - 5mm [color="Red (633nm)" package="5 mm [THT]"]
  LED2 = LED - 5mm [color="Green (555nm)" package="5 mm [THT]"]
  LED3 = LED - 5mm [color="Yellow (595nm)" package="5 mm [THT]"]
  Part1 = Arduino Uno (Rev3)
  R1 = Resistor [tolerance=±5% resistance=1k package=THT]
  R2 = Resistor [tolerance=±5% resistance=1k package=THT]
  R3 = Resistor [tolerance=±5% resistance=1k package=THT]
  part = NPN-Transistor [part_number=2n3904 package="SOT-23 [SMD]"]
  part_2 = NPN-Transistor [part_number=2n3904 package="SOT-23 [SMD]"]
  part_3 = NPN-Transistor [part_number=2n3904 package="SOT-23 [SMD]"]
  R4 = Resistor [tolerance=±5% resistance=100 package=THT]
  R5 = Resistor [tolerance=±5% resistance=100 package=THT]
  R6 = Resistor [tolerance=±5% resistance=100 package=THT]
  BAT1 = Battery Holders [package=lipo-1100mAh]
  BAT2 = Battery Holders [package=lipo-1100mAh]

nets:
  N1: LED1.cathode, R4.Pin_1
  N2: LED1.anode, LED2.anode, LED3.anode, Part1.VIN, BAT1.+
  N3: LED2.cathode, R6.Pin_1
  N4: LED3.cathode, R5.Pin_1
  N5: Part1.D11_PWM/MOSI, R3.Pin_1
  N6: Part1.D12/MISO, R2.Pin_1
  N7: Part1.D13/SCK, R1.Pin_1
  N8: Part1.GND, part.2, part_2.2, part_3.2, BAT2.-
  N9: R1.Pin_0, part.0
  N10: R2.Pin_0, part_2.0
  N11: R3.Pin_0, part_3.0
  N12: part.1, R4.Pin_0
  N13: part_2.1, R5.Pin_0
  N14: part_3.1, R6.Pin_0
  N15: BAT1.-, BAT2.+
